# Fritzing sketch esphome sound thermometer (saved by Fritzing 1.0.4)
breadboards: 2

parts:
  A1 = Esp32-c3 super mini
  U1 = LIPO-1000mAh [package=lipo-1000]
  TP1 = TP4056 [chip_label=TP4056 package="DIP (Dual Inline) [THT]"]
  MOD1 = MT3608/B6289 Boost Module
  S1 = SPST Switch [package=switche-dpdt]
  Q1 = Basic FET P-Channel [package="DPak [SMD]"]
  R1 = Resistor [tolerance=±5% power=0.25W resistance=10k package=THT]
  MIC1 = MAX4466 Electret Microphone Breakout Board
  Part1 = ws2812b [package="smd 2812b"]
  D1 = Schottky Diode [part_number=1N5817 package="Melf DO-213 AB [SMD]"]

nets:
  N1: A1.Pin_9, MIC1.out
  N2: A1.Pin_10, Part1.DIN
  N3: A1.Pin_15, TP1.pin6, MOD1.IN_(-), MOD1.OUT_(-), R1.Pin_1, MIC1.GND
  VCC: A1.Pin_16, MOD1.OUT_(+), MIC1.VCC, Part1.VSS
  N4: U1.+, TP1.pin4
  N5: U1.-, TP1.pin5
  N6: TP1.pin1, Q1.Gate, R1.Pin_0, D1.anode
  N7: TP1.pin3, Q1.drain
  N8: MOD1.IN_(+), S1.S
  N9: S1.P, Q1.source, D1.cathode

custom parts:
  Esp32-c3 super mini: ESP32-C3 Development Board ESP32 SuperMini Development Board ESP32 Development Board WiFi Bluetooth.
  TP4056: A DIP stand-in part for whatever IC you want. With 6 pins on a 300mil dual inline package (DIP) footprint.
  MT3608/B6289 Boost Module: Chip- MT3608 / B6289 DC to DC step up, power booster module. With adjustable output voltage. Current- 2A . || Input voltage- 2V-24V || Output voltage- 5V-28V Input interface- MICRO USB || Inversed polarity- NO. || Led indicator- No.
  MAX4466 Electret Microphone Breakout Board: MAX4466 Electrec Microphone Breakout Board
